# Fritzing sketch Circuit (saved by Fritzing 0.9.3b)

parts:
  U1 = NodeMCU V1.0
  S1 = SPST Switch [package=r_sw_th]
  DHT1 = DHT11 Humitidy and Temperature Sensor
  J1 = Power Jack [package=power_jack_smd]

nets:
  N1: U1.D2, DHT1.DATA
  GND: U1.GND, DHT1.GND, J1.GND
  3V3: U1.3V3, DHT1.VDD
  N2: U1.Vin, S1.O
  N3: S1.P, J1.PWR

custom parts:
  NodeMCU V1.0: ESP8266 based NodeMCU
  DHT11 Humitidy and Temperature Sensor: DHT11 Humidity and Temperature Sensor
